# Fritzing sketch NanoBotArduino (saved by Fritzing 0.9.3b)

parts:
  Componente1 = Arduino Uno (Rev3)
  HC-SR04_Sensor_1 = HC-SR04 Ultrasonic Distance Sensor
  Componente2 = Arduino Motor Shield
  M1 = DC Motor
  M2 = DC Motor
  LED1 = smd LED [color="Red (633nm)" package="1206 [SMD]"]
  R1 = Resistor [tolerance=±5% resistance=220 package=THT]

nets:
  N1: Componente1.D10_PWM/SS, R1.Pin_0
  N2: Componente1.D11_PWM/MOSI, Componente2.OUT3, M1.pin_1
  N3: Componente1.D12/MISO, Componente2.OUT1, M2.pin_2
  N4: Componente1.D13/SCK, Componente2.OUT4, M1.pin_2
  GND: Componente1.GND, HC-SR04_Sensor_1.GND, LED1.cathode
  N5: Componente1.D3_PWM, Componente2.OUT2, M2.pin_1
  N6: Componente1.D4, HC-SR04_Sensor_1.ECHO
  N7: Componente1.D5_PWM, HC-SR04_Sensor_1.TRIG
  5V: Componente1.5V, HC-SR04_Sensor_1.VCC
  N8: LED1.anode, R1.Pin_1
